// Logisim project AND GATE.circ as structural Verilog: 1 circuit, main circuit main
module main (
  input  A,
  input  B
);

  wire AND_out;

  and AND (AND_out, A, B);
  // Probe on AND_out
endmodule
