// Logisim project HALF ADDER.circ as structural Verilog: 1 circuit, main circuit main
module main (
  input  A,
  input  B
);

  wire AND_out, XOR_out;

  xor XOR (XOR_out, A, B);
  and AND (AND_out, B, A);
  // Probe on XOR_out
  // Probe on AND_out
endmodule
