// Logisim project NAND GATE.circ as structural Verilog: 1 circuit, main circuit main
module main (
  input  A,
  input  B
);

  wire NAND_out;

  nand NAND (NAND_out, A, B);
  // Probe on NAND_out
endmodule
