// Logisim project NOR GATE.circ as structural Verilog: 1 circuit, main circuit main
module main (
  input  A,
  input  B
);

  wire NOR_out;

  nor NOR (NOR_out, A, B);
  // Probe on NOR_out
endmodule
