// Logisim project XOR GATE.circ as structural Verilog: 1 circuit, main circuit main
module main (
  input  A,
  input  B
);

  wire XOR_out;

  xor XOR (XOR_out, A, B);
  // Probe on XOR_out
endmodule
